# Fritzing sketch Keyboard_basic_input_pullup (saved by Fritzing 0.9.10b)
breadboards: 1

parts:
  LED2 = LED - 3mm [color="Red (633nm)" current=0.030 package="3 mm [THT]"]
  Componente1 = Arduino Micro (Rev3)
  R1 = Resistor [tolerance=±5% power=0.25 resistance=220 package=THT]
  S1 = Pushbutton [package="[THT]"]

nets:
  N1: LED2.cathode, Componente1.GND, S1.Pin_1, S1.Pin_2
  N2: LED2.anode, R1.Pin_0
  N3: Componente1.D2/SDA, S1.Pin_3, S1.Pin_4
  N4: Componente1.D11_PWM, R1.Pin_1
