# Fritzing sketch pulsante reg stato (saved by Fritzing 0.9.10b)
breadboards: 1

parts:
  Componente1 = Arduino Micro (Rev3)
  LED1 = RGB LED (com. anode, rbg) [package="5 mm [THT]"]
  R1 = Resistor [tolerance=±5% power=0.25 resistance=220 package=THT]
  R2 = Resistor [tolerance=±5% power=0.25 resistance=220 package=THT]
  R3 = Resistor [tolerance=±5% power=0.25 resistance=220 package=THT]
  S1 = Pushbutton [package="[THT]"]
  R4 = Resistor [tolerance=±5% power=0.25 resistance=10 package=THT]

nets:
  N1: Componente1.RESET, LED1.common_anode, S1.Pin_1, S1.Pin_2
  N2: Componente1.D3/SCL, R3.Pin_0
  N3: Componente1.D4_PWM/A6, R2.Pin_0
  N4: Componente1.D5_PWM, R1.Pin_0
  N5: Componente1.D9_PWM/A9, S1.Pin_3, S1.Pin_4, R4.Pin_0
  N6: Componente1.5V, R4.Pin_1
  N7: LED1.red_cathode, R3.Pin_1
  N8: LED1.blue_cathode, R2.Pin_1
  N9: LED1.green_cathode, R1.Pin_1
